# Fritzing sketch lavanderia (saved by Fritzing 0.9.5d)
breadboards: 1

parts:
  WeMos_D1_Mini1 = WeMos D1 Mini  # not connected
  S1 = Pushbutton [package="[THT]"]
  OLED1 = OLED 128x64 I2C Monochrome Display GND-VDD
  J1 = female pin header, 4 pins [form="♀ (female)"]
  Componente1 = ACS712 Current Sensor 5A 20A 30A  # not connected

nets:
  N1: S1.Pin_1, S1.Pin_2, OLED1.GND, J1.pin4
  N2: S1.Pin_3, S1.Pin_4
  N3: OLED1.VDD, J1.pin3
  N4: OLED1.SCK, J1.pin1
  N5: OLED1.SDA, J1.pin2

notes:
  HDC1080
  HDC1080
  SCL|SDA|+|-

custom parts:
  OLED 128x64 I2C Monochrome Display GND-VDD: OLED 128x64 I2C Monochrome Display. Note: there are two variants of this part, this one is the GND VDD SCK SDA variant. The other is VDD GND SCK SDA. Make sure you select the part that matches your module as using the incorrect part will probably destroy your module! In addition the mounting holes are marked on silkscreen but not by default drilled. If you want drilled mounting holes, copy a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
  ACS712 Current Sensor 5A 20A 30A: Remix by Michael Kubina http://www.kubina.info Original by: https://forum.fritzing.org/t/current-sensor-5a-acs712/7694 https://forum.fritzing.org/u/ArtHome ArtHome12@gmail.com
